// Logisim project Processador_finalPulo.circ as structural Verilog: 5 circuits, main circuit main
module main (
  output [3:0] out_1
);

  wire CLK, DADOS, LOAD_raw_out, MOV, not_1_out, not_2_out, not_3_out, STORE_raw_out;
  wire [2:0] OP;
  wire [2:2] RA;
  wire [3:0] alu_1_o, Contador_q, Contador_q_2, controlled_buffer_1_out, INP, O, regfile_1_a, regfile_1_b;
  wire [7:0] ENDR, multiplexer_1_out;
  wire [15:0] rom_1_data;
  wire [15:9] Registrador_de_instrucoes_q;

  Clock clock_1 (.out(CLK));
  Counter Contador (
    .clr(1'b0), .load(1'b0), .up(1'b1), .count(1'b1), .clk(CLK), .Q({Contador_q_2, Contador_q}));  // open: D, carry
  assign controlled_buffer_1_out = MOV ? ENDR[6:3] : 4'bz;  // Controlled_Buffer controlled_buffer_1
  assign controlled_buffer_1_out = DADOS ? alu_1_o : 4'bz;  // Controlled_Buffer controlled_buffer_2
  REGFILE regfile_1 (
    .RA({RA[2], ENDR[7:6]}), .RB(ENDR[5:3]), .RD(ENDR[2:0]), .INP(controlled_buffer_1_out), .CLK(CLK),
    .A(regfile_1_a), .B(regfile_1_b));
  Hex_Digit_Display hex_digit_display_1 (.value(Contador_q_2));  // open: dp
  ROM #(.dataWidth(16)) rom_1 (.addr({Contador_q_2, Contador_q}), .data(rom_1_data));
  not not_1 (not_1_out, OP[0]);
  not not_2 (not_2_out, OP[1]);
  not not_3 (not_3_out, OP[2]);
  Hex_Digit_Display hex_digit_display_2 (.value(Contador_q));  // open: dp
  ALU alu_1 (.A(regfile_1_a), .B(regfile_1_b), .OP(OP), .O(alu_1_o));
  LED led_1 (.in(STORE_raw_out));
  and STORE_raw (STORE_raw_out, not_1_out, OP[1], OP[2]);
  and LOAD_raw (LOAD_raw_out, OP[0], not_2_out, not_3_out);
  LED led_2 (.in(LOAD_raw_out));
  Multiplexer #(.width(8)) multiplexer_1 (
    .in0({Contador_q_2, Contador_q}), .in1(ENDR), .out(multiplexer_1_out), .sel(LOAD_raw_out));
  Register #(.width(16)) Registrador_de_instrucoes (
    .D(rom_1_data), .en(1'b1), .clk(CLK),
    .Q({Registrador_de_instrucoes_q[15:14], OP, Registrador_de_instrucoes_q[10:9], RA[2], ENDR}));  // open: clr
  RAM #(.dataWidth(4)) ram_1 (
    .addr(multiplexer_1_out), .we(STORE_raw_out), .oe(LOAD_raw_out), .clk(CLK), .din(ENDR[6:3]), .dout(out_1));
  and and_1 (DADOS, ~Registrador_de_instrucoes_q[14], ~Registrador_de_instrucoes_q[15]);  // AND_Gate
  and and_2 (MOV, Registrador_de_instrucoes_q[14], Registrador_de_instrucoes_q[15]);
  Multiplexer #(.select(3), .width(4)) multiplexer_2 (
    .in0(O), .in1(ENDR[6:3]), .in2(out_1), .out(INP), .sel(OP));  // open: in3, in4, in5, in6, in7

  // Other names for the same wires on the sheet: RD[2:0] = ENDR[2:0]; NUM[3:0] = ENDR[6:3]; RB[2:0] = ENDR[5:3];
  //   RA[1:0] = ENDR[7:6]; OP2 = OP[0]; OP0 = OP[2]

  // Notes on the sheet:
  //   contents of rom_1 (hex, n*v repeats v):
  //   c019 c010 f019 f021 c804 c803
endmodule

module ALU (
  input  [3:0] A,
  input  [3:0] B,
  input  [2:0] OP,
  output [3:0] O
);

  wire [3:0] adder_1_out, and_1_out, multiplier_1_out, or_1_out, shifter_1_out, shifter_2_out,
       subtractor_1_out, xor_1_out;

  Adder #(.width(4)) adder_1 (.a(A), .b(B), .out(adder_1_out), .cin(1'b0));  // open: cout
  Subtractor #(.width(4)) subtractor_1 (.a(A), .b(B), .out(subtractor_1_out), .bin(1'b0));  // open: bout
  assign and_1_out = A & B;  // AND_Gate and_1, 4 bits wide
  assign or_1_out = A | B;  // OR_Gate or_1, 4 bits wide
  assign xor_1_out = A ^ B;  // XOR_Gate xor_1, 4 bits wide
  Shifter #(.width(4)) shifter_1 (.in(A), .\dist (2'b01), .out(shifter_1_out));
  Shifter #(.shift("lr"), .width(4)) shifter_2 (.in(A), .\dist (2'b01), .out(shifter_2_out));
  Multiplier #(.width(4)) multiplier_1 (.a(A), .b(B), .out(multiplier_1_out));  // open: cin, cout
  Multiplexer #(.enable("true"), .select(3), .width(4)) multiplexer_1 (
    .in0(adder_1_out), .in1(subtractor_1_out), .in2(and_1_out), .in3(or_1_out), .in4(xor_1_out),
    .in5(shifter_1_out), .in6(shifter_2_out), .in7(multiplier_1_out), .out(O), .sel(OP));  // open: en
endmodule

module REGFILE (
  input  [3:0] INP,
  input  CLK,
  input  [2:0] RA,
  input  [2:0] RD,
  input  [2:0] RB,
  output [3:0] A,
  output [3:0] B
);

  wire demultiplexer_1_out0, demultiplexer_1_out1, demultiplexer_1_out2, demultiplexer_1_out3,
       demultiplexer_1_out4, demultiplexer_1_out5, demultiplexer_1_out6, demultiplexer_1_out7;
  wire [3:0] R0_q, R1_q, R2_q, R3_q, R4_q, R5_q, R6_q, R7_q;

  Demultiplexer #(.enable("true"), .select(3)) demultiplexer_1 (
    .out0(demultiplexer_1_out0), .out1(demultiplexer_1_out1), .out2(demultiplexer_1_out2),
    .out3(demultiplexer_1_out3), .out4(demultiplexer_1_out4), .out5(demultiplexer_1_out5),
    .out6(demultiplexer_1_out6), .out7(demultiplexer_1_out7), .in(1'b1), .sel(RD));  // open: en
  Register #(.width(4)) R0 (.D(INP), .en(demultiplexer_1_out0), .clk(CLK), .Q(R0_q));  // open: clr
  Register #(.width(4)) R1 (.D(INP), .en(demultiplexer_1_out1), .clk(CLK), .Q(R1_q));  // open: clr
  Register #(.width(4)) R2 (.D(INP), .en(demultiplexer_1_out2), .clk(CLK), .Q(R2_q));  // open: clr
  Register #(.width(4)) R3 (.D(INP), .en(demultiplexer_1_out3), .clk(CLK), .Q(R3_q));  // open: clr
  Register #(.width(4)) R4 (.D(INP), .en(demultiplexer_1_out4), .clk(CLK), .Q(R4_q));  // open: clr
  Register #(.width(4)) R5 (.D(INP), .en(demultiplexer_1_out5), .clk(CLK), .Q(R5_q));  // open: clr
  Register #(.width(4)) R6 (.D(INP), .en(demultiplexer_1_out6), .clk(CLK), .Q(R6_q));  // open: clr
  Register #(.width(4)) R7 (.D(INP), .en(demultiplexer_1_out7), .clk(CLK), .Q(R7_q));  // open: clr
  Multiplexer #(.enable("true"), .select(3), .width(4)) multiplexer_1 (
    .in0(R0_q), .in1(R1_q), .in2(R2_q), .in3(R3_q), .in4(R4_q), .in5(R5_q), .in6(R6_q), .in7(R7_q), .out(A),
    .sel(RA));  // open: en
  Multiplexer #(.enable("true"), .select(3), .width(4)) multiplexer_2 (
    .in0(R0_q), .in1(R1_q), .in2(R2_q), .in3(R3_q), .in4(R4_q), .in5(R5_q), .in6(R6_q), .in7(R7_q), .out(B),
    .sel(RB));  // open: en
endmodule

module ALU1 (
  input  [3:0] A,
  input  [3:0] B,
  input  [1:0] OP,
  output [3:0] O
);

  wire [3:0] adder_1_out, and_1_out, or_1_out, xor_1_out;

  Adder #(.width(4)) adder_1 (.a(A), .b(B), .out(adder_1_out), .cin(1'b0));  // open: cout
  assign and_1_out = A & B;  // AND_Gate and_1, 4 bits wide
  assign or_1_out = A | B;  // OR_Gate or_1, 4 bits wide
  assign xor_1_out = A ^ B;  // XOR_Gate xor_1, 4 bits wide
  Multiplexer #(.enable("true"), .select(2), .width(4)) multiplexer_1 (
    .in0(adder_1_out), .in1(and_1_out), .in2(or_1_out), .in3(xor_1_out), .out(O), .sel(OP));  // open: en
endmodule

module sapo (
  input  [3:0] in_1,
  output [3:0] out_2
);

  wire CLK;
  wire [7:0] counter_1_q;

  Clock clock_1 (.out(CLK));
  Counter counter_1 (.D(8'h1), .Q(counter_1_q), .clk(CLK));  // open: load, count, carry, up, clr
  RAM #(.dataWidth(4)) ram_1 (.addr(counter_1_q), .we(CLK), .clk(CLK), .din(in_1), .dout(out_2));  // open: oe
endmodule
